# Fritzing sketch clockgenerator (saved by Fritzing 0.9.2b)
breadboards: 1

parts:
  Part1 = Si5351A Clock Generator
  Grove1 = Grove OLED 128x96
  CLK0 = SMA Antenna Connector [package=sma-edge]
  Part3 = Arduino Uno (Rev3)
  CLK1 = SMA Antenna Connector [package=sma-edge]
  CLK2 = SMA Antenna Connector [package=sma-edge]
  CLK3 = SMA Antenna Connector [package=sma-edge]
  ENCODER1 = Rotary Encoder with Knob
  R1 = Resistor [tolerance=±5% resistance=120 package=THT]
  R2 = Resistor [tolerance=±5% resistance=220 package=THT]
  R3 = Resistor [tolerance=±5% resistance=220 package=THT]
  R4 = Resistor [tolerance=±5% resistance=220 package=THT]
  CLKSEL = Pushbutton [package="[THT]"]
  SAVE = Pushbutton [package="[THT]"]

nets:
  VIN: Part1.VIN, Grove1.VCC, Part3.5V, ENCODER1.no_name_yet#4, CLKSEL.Pin_1, CLKSEL.Pin_2, SAVE.Pin_1, SAVE.Pin_2
  GND: Part1.GND#11, Grove1.GND, Part3.GND, CLK3.GND, ENCODER1.no_name_yet#3, R2.Pin_1, R3.Pin_1, R4.Pin_1
  N1: Part1.SDA, Grove1.SDA, Part3.A4/SDA
  N2: Part1.SCL, Grove1.SCL, Part3.A5/SCL
  N3: Part1.GND#51, CLK2.GND
  N4: Part1.CLK0#52, CLK2.SIGNAL
  N5: Part1.GND#56, CLK1.GND
  N6: Part1.CLK1#57, CLK1.SIGNAL
  N7: Part1.GND#61, CLK0.GND
  N8: Part1.CLK2#62, CLK0.SIGNAL
  N9: Part3.D9_PWM, R1.Pin_0
  N10: Part3.D2, ENCODER1.no_name_yet#2
  N11: Part3.D3_PWM, ENCODER1.no_name_yet#1
  N12: Part3.D4, ENCODER1.no_name_yet#5, R3.Pin_0
  N13: Part3.D5_PWM, R2.Pin_0, CLKSEL.Pin_3, CLKSEL.Pin_4
  N14: Part3.D6_PWM, R4.Pin_0, SAVE.Pin_3, SAVE.Pin_4
  N15: CLK3.SIGNAL, R1.Pin_1

custom parts:
  Si5351A Clock Generator: The Si5351A clock generator is an I2C controller clock generator. It uses the onboard precision clock to drive multiple PLL's and clock dividers using I2C instructions. By setting up the PLL and dividers you can create precise and arbitrary frequencies. There are three independent outputs, and each one can have a different frequency. Outputs are 3Vpp, either through a breadboard-friendly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
  Rotary Encoder with Knob: Rotary Encoder with 1/4" Shaft and Knob
